// Logisim project cpu.circ as structural Verilog: 3 circuits, main circuit ALU
module datapath (
  input  [7:0] Input,
  input  RST,
  output halt,
  output [7:0] Out
);

  wire A_Enable, B_Enable, CLK, MBR_Enable, Out_Enable, PC_Enable;
  wire [1:0] B_Select;
  wire [2:0] ALU_Select;
  wire [7:0] A_q, ALU_out, B_q, Data, MBR_q, multiplexer_1_out, PC_q;

  Clock u_CLK (.out(CLK));
  Register A (.D(ALU_out), .en(A_Enable), .Q(A_q), .clk(CLK), .clr(RST));
  Register B (.D(ALU_out), .en(B_Enable), .Q(B_q), .clk(CLK), .clr(RST));
  Register MBR (.D(Data), .en(MBR_Enable), .Q(MBR_q), .clk(CLK), .clr(RST));
  Register PC (.D(ALU_out), .en(PC_Enable), .Q(PC_q), .clk(CLK), .clr(RST));
  Register u_Out (.D(ALU_out), .en(Out_Enable), .Q(Out), .clk(CLK), .clr(RST));
  Multiplexer #(.select(2), .width(8)) multiplexer_1 (
    .in0(B_q), .in1(MBR_q), .in2(PC_q), .in3(Input), .out(multiplexer_1_out), .sel(B_Select));  // open: en
  Hex_Digit_Display hex_digit_display_1 (.value(Out[3:0]));  // open: dp
  Hex_Digit_Display hex_digit_display_2 (.value(Out[7:4]));  // open: dp
  control Control_Unit (
    .RST(RST), .From_MBR(MBR_q[4:0]),
    .Write_enables({A_Enable, B_Enable, MBR_Enable, PC_Enable, Out_Enable}), .B_Select(B_Select),
    .ALU_Select(ALU_Select), .Halt(halt));
  ALU ALU (.A(A_q), .B(multiplexer_1_out), .S(ALU_Select), .Out(ALU_out));  // open: ZF, VF
  RAM #(.bus("asynch")) ram_1 (.addr(PC_q), .data(Data));  // open: sel, ld, clr
endmodule

module ALU (
  input  [7:0] A,
  input  [7:0] B,
  input  [2:0] S,
  output [7:0] Out,
  output ZF,
  output VF
);

  wire A_B, A_B_t, A_plus_plus, and_1_out, and_2_out, and_3_out, B_plus_plus, nor_1_out, not_1_out,
       not_3_out, or_1_out, or_2_out;
  wire [7:0] and_5_out, multiplexer_1_out, not_2_out, or_3_out, plus_In1, plus_In2, plus_Out;

  Decoder #(.select(3)) decoder_1 (
    .out2(A_plus_plus), .out3(B_plus_plus), .out4(A_B), .out5(A_B_t), .sel(S));  // open: out0, out1, out6, out7, en
  or or_1 (or_1_out, A_B_t, A_B, B_plus_plus, A_plus_plus);
  and and_1 (and_1_out, plus_In1[7], plus_In2[7]);
  nor nor_1 (nor_1_out, plus_In1[7], plus_In2[7]);
  not not_1 (not_1_out, plus_Out[7]);
  assign not_2_out = ~B;  // NOT_Gate not_2, 8 bits wide
  and and_2 (and_2_out, and_1_out, not_1_out);
  and and_3 (and_3_out, nor_1_out, plus_Out[7]);
  Multiplexer #(.width(8)) multiplexer_1 (.in0(B), .in1(not_2_out), .out(multiplexer_1_out), .sel(A_B_t));  // open: en
  Multiplexer #(.width(8)) multiplexer_2 (.in0(A), .in1(8'h1), .out(plus_In1), .sel(B_plus_plus));  // open: en
  Multiplexer #(.width(8)) multiplexer_3 (
    .in0(8'h1), .in1(multiplexer_1_out), .out(plus_In2), .sel(not_3_out));  // open: en
  not not_3 (not_3_out, A_plus_plus);
  and and_4 (VF, or_1_out, or_2_out);
  or or_2 (or_2_out, and_2_out, and_3_out);
  Adder adder_1 (.a(plus_In1), .b(plus_In2), .out(plus_Out), .cin(A_B_t));  // open: cout
  assign and_5_out = A & B;  // AND_Gate and_5, 8 bits wide
  assign or_3_out = A | B;  // OR_Gate or_3, 8 bits wide
  Multiplexer #(.select(3), .width(8), .enable("false")) multiplexer_4 (
    .in0(A), .in1(B), .in2(plus_Out), .in3(plus_Out), .in4(plus_Out), .in5(plus_Out), .in6(and_5_out),
    .in7(or_3_out), .out(Out), .sel(S));
  nor nor_2 (ZF, Out[0], Out[1], Out[2], Out[3], Out[4], Out[5], Out[6], Out[7]);
endmodule

module control (
  input  RST,
  input  [4:0] From_MBR,
  output [4:0] Write_enables,
  output [1:0] B_Select,
  output [2:0] ALU_Select,
  output Halt
);

  wire CLK_out;
  wire [4:0] IR_q, multiplexer_1_out, SPC_q, xnor_1_out;
  wire [10:10] IR_q_2;
  wire [15:0] rom_1_data;

  Clock CLK (.out(CLK_out));
  Multiplexer #(.width(5)) multiplexer_1 (
    .in0(IR_q), .in1(From_MBR), .out(multiplexer_1_out), .sel(IR_q_2[10]));  // open: en
  Register #(.width(5)) SPC (.D(multiplexer_1_out), .Q(SPC_q), .clk(CLK_out), .clr(RST));  // open: en
  ROM #(.addrWidth(5), .dataWidth(16)) rom_1 (.addr(SPC_q), .data(rom_1_data));  // open: sel
  Register #(.width(16), .trigger("falling")) IR (
    .D(rom_1_data), .Q({IR_q, IR_q_2[10], ALU_Select, B_Select, Write_enables}), .clk(CLK_out), .clr(RST));  // open: en
  assign xnor_1_out = ~(SPC_q ^ 5'b11101);  // XNOR_Gate xnor_1, 5 bits wide
  and and_1 (Halt, xnor_1_out[0], xnor_1_out[1], xnor_1_out[2], xnor_1_out[3], xnor_1_out[4]);

  // Notes on the sheet:
  //   contents of rom_1 (hex, n*v repeats v):
  //   804 11c0 19c2 400 28e0 30f0 0 4000 4801 0 5804 60a0 68a2 0 7804 81c0 89c2 90a0 98b0 0 a900 b110 0
  //   c000 c808 0 da00 e210 0 e800
endmodule
